// Logisim project xetroc.circ as structural Verilog: 13 circuits, main circuit main
module main (
);

  wire arm_control_unit_1_alusrc, arm_control_unit_1_memtoreg, arm_control_unit_1_memwrite,
       arm_control_unit_1_pcsrc, arm_control_unit_1_regwrite, clk, reset;
  wire [1:0] arm_control_unit_1_alucontrol, arm_control_unit_1_immsrc;
  wire [2:0] arm_control_unit_1_regsrc;
  wire [3:0] alu_1_aluflags, registerselect_1_ra1, registerselect_1_ra2, registerselect_1_ra3;
  wire [15:0] rom_1_data;
  wire [31:0] adder_1_out, adder_2_out, alu_1_result, immediate_1_imm32, multiplexer_1_out,
       multiplexer_2_out, multiplexer_3_out, PC_q, ram_1_dout, registerfile_1_rd1, registerfile_1_rd2;

  Button u_reset (.out(reset));
  Clock u_clk (.out(clk));
  Register #(.width(32)) PC (.D(multiplexer_1_out), .en(1'b1), .clk(clk), .Q(PC_q), .clr(reset));
  Multiplexer #(.width(32)) multiplexer_1 (
    .in0(adder_1_out), .in1(multiplexer_3_out), .out(multiplexer_1_out), .sel(arm_control_unit_1_pcsrc));
  ROM #(.addrWidth(16), .dataWidth(16)) rom_1 (.addr(PC_q[16:1]), .data(rom_1_data));
  Adder #(.width(32)) adder_1 (.a(PC_q), .b(32'h2), .out(adder_1_out));  // open: cin, cout
  ARM_Control_Unit arm_control_unit_1 (
    .Clk(clk), .ALUFlags(alu_1_aluflags), .instruction(rom_1_data), .PCSrc(arm_control_unit_1_pcsrc),
    .MemToReg(arm_control_unit_1_memtoreg), .MemWrite(arm_control_unit_1_memwrite),
    .ALUControl(arm_control_unit_1_alucontrol), .ALUSrc(arm_control_unit_1_alusrc),
    .ImmSrc(arm_control_unit_1_immsrc), .RegWrite(arm_control_unit_1_regwrite),
    .RegSrc(arm_control_unit_1_regsrc));
  RegisterSelect registerselect_1 (
    .RegSel(arm_control_unit_1_regsrc), .instr(rom_1_data), .RA1(registerselect_1_ra1),
    .RA2(registerselect_1_ra2), .RA3(registerselect_1_ra3));
  Adder #(.width(32)) adder_2 (.a(adder_1_out), .b(32'h2), .out(adder_2_out));  // open: cin, cout
  RegisterFile registerfile_1 (
    .A1(registerselect_1_ra1), .A2(registerselect_1_ra2), .A3(registerselect_1_ra3),
    .WE3(arm_control_unit_1_regwrite), .WD3(multiplexer_3_out), .clk(clk), .R15(adder_2_out),
    .RD1(registerfile_1_rd1), .RD2(registerfile_1_rd2));
  Immediate immediate_1 (.op(arm_control_unit_1_immsrc), .inst(rom_1_data), .imm32(immediate_1_imm32));
  Multiplexer #(.width(32)) multiplexer_2 (
    .in0(registerfile_1_rd2), .in1(immediate_1_imm32), .out(multiplexer_2_out),
    .sel(arm_control_unit_1_alusrc));
  ALU alu_1 (
    .B(registerfile_1_rd1), .A(multiplexer_2_out), .ALUControl(arm_control_unit_1_alucontrol),
    .Result(alu_1_result), .ALUFlags(alu_1_aluflags));
  RAM #(.addrWidth(16), .dataWidth(32)) ram_1 (
    .addr(alu_1_result[17:2]), .we(arm_control_unit_1_memwrite), .oe(1'b1), .clk(clk),
    .din(registerfile_1_rd2), .dout(ram_1_dout));
  Multiplexer #(.width(32)) multiplexer_3 (
    .in0(alu_1_result), .in1(ram_1_dout), .out(multiplexer_3_out), .sel(arm_control_unit_1_memtoreg));

  // Notes on the sheet:
  //   contents of rom_1 (hex, n*v repeats v):
  //   2004 1 d003 3901 d001 1840 e7fb e7fe
endmodule

module RegisterFile (
  input  [3:0] A1,
  input  [3:0] A2,
  input  [3:0] A3,
  input  WE3,
  input  [31:0] WD3,
  input  clk,
  input  [31:0] R15,
  output [31:0] RD1,
  output [31:0] RD2
);

  wire decoder_1_out0, decoder_1_out1, decoder_1_out2, decoder_1_out3, decoder_1_out4, decoder_1_out5,
       decoder_1_out6, decoder_1_out7;
  wire [31:0] R0_q, R1_q, R2_q, R3_q, R4_q, R5_q, R6_q, R7_q;

  Decoder #(.select(4)) decoder_1 (
    .out0(decoder_1_out0), .out1(decoder_1_out1), .out2(decoder_1_out2), .out3(decoder_1_out3),
    .out4(decoder_1_out4), .out5(decoder_1_out5), .out6(decoder_1_out6), .out7(decoder_1_out7), .sel(A3),
    .en(WE3));  // open: out8, out9, out10, out11, out12, out13, out14, out15
  Register #(.width(32)) R0 (.D(WD3), .en(decoder_1_out0), .clk(clk), .Q(R0_q));  // open: clr
  Register #(.width(32)) R1 (.D(WD3), .en(decoder_1_out1), .clk(clk), .Q(R1_q));  // open: clr
  Register #(.width(32)) R2 (.D(WD3), .en(decoder_1_out2), .clk(clk), .Q(R2_q));  // open: clr
  Register #(.width(32)) R3 (.D(WD3), .en(decoder_1_out3), .clk(clk), .Q(R3_q));  // open: clr
  Register #(.width(32)) R4 (.D(WD3), .en(decoder_1_out4), .clk(clk), .Q(R4_q));  // open: clr
  Register #(.width(32)) R5 (.D(WD3), .en(decoder_1_out5), .clk(clk), .Q(R5_q));  // open: clr
  Register #(.width(32)) R6 (.D(WD3), .en(decoder_1_out6), .clk(clk), .Q(R6_q));  // open: clr
  Register #(.width(32)) R7 (.D(WD3), .en(decoder_1_out7), .clk(clk), .Q(R7_q));  // open: clr
  Multiplexer #(.select(4), .width(32)) multiplexer_1 (
    .in0(R0_q), .in1(R1_q), .in2(R2_q), .in3(R3_q), .in4(R4_q), .in5(R5_q), .in6(R6_q), .in7(R7_q),
    .in15(R15), .out(RD1), .sel(A1));  // open: in8, in9, in10, in11, in12, in13, in14
  Multiplexer #(.select(4), .width(32)) multiplexer_2 (
    .in0(R0_q), .in1(R1_q), .in2(R2_q), .in3(R3_q), .in4(R4_q), .in5(R5_q), .in6(R6_q), .in7(R7_q),
    .in15(R15), .out(RD2), .sel(A2));  // open: in8, in9, in10, in11, in12, in13, in14
endmodule

module ALU (
  input  [1:0] ALUControl,
  input  [31:0] B,
  input  [31:0] A,
  output [31:0] Result,
  output [3:0] ALUFlags
);

  wire adder_32_bit_1_carryout, not_2_out, Sum31, xnor_1_out, xor_1_out;
  wire [30:0] adder_32_bit_1_sum;
  wire [31:0] and_1_out, multiplexer_1_out, not_1_out, or_1_out;

  assign not_1_out = ~B;  // NOT_Gate not_1, 32 bits wide
  Multiplexer #(.width(32)) multiplexer_1 (.in0(B), .in1(not_1_out), .out(multiplexer_1_out), .sel(ALUControl[0]));
  assign and_1_out = B & A;  // AND_Gate and_1, 32 bits wide
  assign or_1_out = B | A;  // OR_Gate or_1, 32 bits wide
  not not_2 (not_2_out, ALUControl[1]);
  xor xor_1 (xor_1_out, Sum31, A[31]);
  NotExactlyOne xnor_1 (.out(xnor_1_out), .in0(A[31]), .in1(B[31]), .in2(ALUControl[0]));
  Adder_32_bit adder_32_bit_1 (
    .A(multiplexer_1_out), .B(A), .CarryIn(ALUControl[0]), .CarryOut(adder_32_bit_1_carryout),
    .Sum({Sum31, adder_32_bit_1_sum}));
  Multiplexer #(.select(2), .width(32)) multiplexer_2 (
    .in0({Sum31, adder_32_bit_1_sum}), .in1({Sum31, adder_32_bit_1_sum}), .in2(and_1_out), .in3(or_1_out),
    .out({ALUFlags[3], Result[30:0]}), .sel(ALUControl));
  and and_2 (ALUFlags[1], adder_32_bit_1_carryout, not_2_out);
  and and_3 (ALUFlags[0], not_2_out, xor_1_out, xnor_1_out);
  Zero_Detect_32_bit Zero_Detect (.A({ALUFlags[3], Result[30:0]}), .B(ALUFlags[2]));

  assign Result[31] = ALUFlags[3];

  // Notes on the sheet:
  //   00 ADD
  //   01 SUB
  //   10 AND
  //   11 OR
  //   Negative
  //   Carry
  //   oVerflow
  //   Zero
  //   NZCV
endmodule

module Immediate (
  input  [1:0] op,
  input  [15:0] inst,
  output [31:0] imm32
);

  wire [31:0] bit_extender_1_out, bit_extender_2_out, bit_extender_3_out;

  assign bit_extender_1_out = {{24{1'b0}}, inst[7:0]};  // Bit_Extender bit_extender_1
  assign bit_extender_2_out = {{24{inst[7]}}, inst[7:0]};  // Bit_Extender bit_extender_2
  assign bit_extender_3_out = {{21{inst[10]}}, inst[10:0]};  // Bit_Extender bit_extender_3
  Multiplexer #(.select(2), .width(32)) multiplexer_1 (
    .in0({32{1'b0}}), .in1(bit_extender_1_out), .in2(bit_extender_2_out), .in3(bit_extender_3_out),
    .out(imm32), .sel(op));

  // Notes on the sheet:
  //   01 imm8
  //   10 simm8
  //   11 simm11
endmodule

module ARM_Condition_Check (
  input  [3:0] Cond,
  input  [3:0] ALUFlags,
  output CondEx
);

  wire and_1_out, and_2_out, not_1_out, not_2_out, not_3_out, not_4_out, not_5_out, not_6_out, not_7_out,
       xor_1_out;

  xor xor_1 (xor_1_out, ALUFlags[3], ALUFlags[0]);
  and and_1 (and_1_out, ~ALUFlags[2], ALUFlags[1]);  // AND_Gate
  not not_1 (not_1_out, xor_1_out);
  and and_2 (and_2_out, not_1_out, ~ALUFlags[2]);  // AND_Gate
  not not_2 (not_2_out, ALUFlags[2]);
  not not_3 (not_3_out, ALUFlags[1]);
  not not_4 (not_4_out, ALUFlags[3]);
  not not_5 (not_5_out, ALUFlags[0]);
  not not_6 (not_6_out, and_1_out);
  not not_7 (not_7_out, and_2_out);
  Multiplexer #(.select(4)) multiplexer_1 (
    .in0(ALUFlags[2]), .in1(not_2_out), .in2(ALUFlags[1]), .in3(not_3_out), .in4(ALUFlags[3]),
    .in5(not_4_out), .in6(ALUFlags[0]), .in7(not_5_out), .in8(and_1_out), .in9(not_6_out), .in10(not_1_out),
    .in11(xor_1_out), .in12(and_2_out), .in13(not_7_out), .in14(1'b1), .out(CondEx), .sel(Cond));  // open: in15

  // Other names for the same wires on the sheet: V = ALUFlags[0]; C = ALUFlags[1]; Z = ALUFlags[2]; N = ALUFlags[3]

  // Notes on the sheet:
  //   Negative
  //   Zero
  //   Carry
  //   oVerflow
endmodule

module ARM_Conditional_Logic (
  input  [3:0] ALUFlags,
  input  [1:0] FlagW,
  input  [3:0] Cond,
  input  MemW,
  input  NoWrite,
  input  RegW,
  input  PCS,
  input  CLK,
  output PCSrc,
  output RegWrite,
  output MemWrite
);

  wire and_1_out, and_2_out, arm_condition_check_1_condex;
  wire [1:0] ALUFlags_01_q, ALUFlags_32_q;

  and and_1 (and_1_out, FlagW[1], arm_condition_check_1_condex);
  and and_2 (and_2_out, FlagW[0], arm_condition_check_1_condex);
  Register #(.width(2)) ALUFlags_32 (.D(ALUFlags[3:2]), .en(and_1_out), .clk(CLK), .Q(ALUFlags_32_q));  // open: clr
  Register #(.width(2)) ALUFlags_01 (.D(ALUFlags[1:0]), .en(and_2_out), .clk(CLK), .Q(ALUFlags_01_q));  // open: clr
  ARM_Condition_Check arm_condition_check_1 (
    .Cond(Cond), .ALUFlags({ALUFlags_32_q, ALUFlags_01_q}), .CondEx(arm_condition_check_1_condex));
  and and_3 (PCSrc, PCS, arm_condition_check_1_condex);
  and and_4 (RegWrite, RegW, ~NoWrite, arm_condition_check_1_condex);  // AND_Gate
  and and_5 (MemWrite, MemW, arm_condition_check_1_condex);

  // Other names for the same wires on the sheet: ALUFlags01[1:0] = ALUFlags[1:0]; ALUFlags32[1:0] = ALUFlags[3:2]
endmodule

module ARM_Decoder (
  input  [15:0] Instruction,
  output [3:0] cond,
  output PCS,
  output MemToReg,
  output MemW,
  output ALUSrc,
  output [1:0] ImmSrc,
  output RegW,
  output [2:0] RegSrc,
  output [1:0] ALUControl,
  output [1:0] FlagW,
  output NoWrite
);

  wire ADDS, ADDSi, B, Bcc, MOVS, MOVSi, or_4_out, or_5_out, STR, SUBS, SUBSi;
  wire [3:0] cond_t;

  and and_1 (MOVS, ~Instruction[15], ~Instruction[14], ~Instruction[13], ~Instruction[12], ~Instruction[11], ~Instruction[10], ~Instruction[9], ~Instruction[8], ~Instruction[7], ~Instruction[6]);  // AND_Gate
  and and_2 (ADDS, ~Instruction[15], ~Instruction[14], ~Instruction[13], Instruction[12], Instruction[11], ~Instruction[10], ~Instruction[9]);  // AND_Gate
  and and_3 (SUBS, ~Instruction[15], ~Instruction[14], ~Instruction[13], Instruction[12], Instruction[11], ~Instruction[10], ~Instruction[9]);  // AND_Gate
  and and_4 (MOVSi, ~Instruction[15], ~Instruction[14], Instruction[13], ~Instruction[12], ~Instruction[11]);  // AND_Gate
  and and_5 (ADDSi, ~Instruction[15], ~Instruction[14], Instruction[13], Instruction[12], ~Instruction[11]);  // AND_Gate
  and and_6 (SUBSi, ~Instruction[15], ~Instruction[14], Instruction[13], Instruction[12], Instruction[11]);  // AND_Gate
  and and_7 (MemToReg, Instruction[15], ~Instruction[14], ~Instruction[13], Instruction[12], Instruction[11]);  // AND_Gate
  and and_8 (STR, Instruction[15], ~Instruction[14], ~Instruction[13], Instruction[12], ~Instruction[11]);  // AND_Gate
  and and_9 (Bcc, Instruction[15], Instruction[14], ~Instruction[13], Instruction[12]);  // AND_Gate
  and and_10 (B, Instruction[15], Instruction[14], Instruction[13], ~Instruction[12], ~Instruction[11]);  // AND_Gate
  Multiplexer #(.width(4)) multiplexer_1 (.in0(4'b1110), .in1(Instruction[15:12]), .out(cond_t), .sel(Bcc));
  Multiplexer #(.width(4)) multiplexer_2 (.in0(4'b1110), .in1(cond_t), .out(cond), .sel(Bcc));
  or or_1 (PCS, Bcc, B);
  or or_2 (ALUSrc, ADDSi, SUBSi, MOVSi);
  or or_3 (RegW, ADDS, SUBS, ADDSi, SUBSi, MOVS, MOVSi, STR);
  or or_4 (or_4_out, ADDS, ADDSi);
  or or_5 (or_5_out, SUBS, SUBSi);
  or or_6 (FlagW[0], ADDS, SUBS, ADDSi, SUBSi);
  Priority_Encoder #(.select(2)) priority_encoder_1 (
    .in1(ALUSrc), .in2(Bcc), .in3(B), .out(ImmSrc));  // open: in0, gs, en_out, en_in
  Priority_Encoder priority_encoder_2 (.out(RegSrc));  // open: in0, in1, in2, in3, in4, in5, in6, in7, en_in, gs, en_out
  Priority_Encoder #(.select(2)) priority_encoder_3 (
    .in0(or_4_out), .in1(or_5_out), .out(ALUControl));  // open: in2, in3, gs, en_out, en_in
  or or_7 (FlagW[1], FlagW[0], MOVS, MOVSi);

  assign NoWrite = 1'b0;

  // Other names for the same wires on the sheet: clk = Instruction[14]; LDR = MemToReg; R_210[2:0] = Instruction[2:0];
  //   R_543[2:0] = Instruction[5:3]; R_987[2:0] = Instruction[8:6]; R_A98[2:0] = Instruction[10:8]

  // Notes on the sheet:
  //   MemWrite before condition checked
  //   select ALU operation
  //   1 for computed PC values, eg branch targets
  //   1 for using RAM ReadData, else ALUResult
  //   0 for using RD2 1 for ExtImm as ALU SrcB
  //   kind of imm exension to ExtImm
  //   select which kind of imm exension to ExtImm
  //   RegWrite before condition checked
  //   1 dont write result to Rd 
  //   select which instruction bits are used for register addresses
  //   01 imm8
  //   10 simm8
  //   11 simm11
  //   FlagW1 for updating N and Z (Flags3:2), and FlagW0 for updating C and V (Flags1:0).
endmodule

module ARM_Control_Unit (
  input  Clk,
  input  [3:0] ALUFlags,
  input  [15:0] instruction,
  output PCSrc,
  output MemToReg,
  output MemWrite,
  output [1:0] ALUControl,
  output ALUSrc,
  output [1:0] ImmSrc,
  output RegWrite,
  output [2:0] RegSrc
);

  wire arm_decoder_1_memw, arm_decoder_1_nowrite, arm_decoder_1_pcs, arm_decoder_1_regw;
  wire [1:0] arm_decoder_1_flagw;
  wire [3:0] arm_decoder_1_cond;

  ARM_Decoder arm_decoder_1 (
    .Instruction(instruction), .cond(arm_decoder_1_cond), .PCS(arm_decoder_1_pcs), .MemToReg(MemToReg),
    .MemW(arm_decoder_1_memw), .ALUSrc(ALUSrc), .ImmSrc(ImmSrc), .RegW(arm_decoder_1_regw), .RegSrc(RegSrc),
    .ALUControl(ALUControl), .FlagW(arm_decoder_1_flagw), .NoWrite(arm_decoder_1_nowrite));
  ARM_Conditional_Logic arm_conditional_logic_1 (
    .ALUFlags(ALUFlags), .FlagW(arm_decoder_1_flagw), .Cond(arm_decoder_1_cond), .MemW(arm_decoder_1_memw),
    .NoWrite(arm_decoder_1_nowrite), .RegW(arm_decoder_1_regw), .PCS(arm_decoder_1_pcs), .CLK(Clk),
    .PCSrc(PCSrc), .RegWrite(RegWrite), .MemWrite(MemWrite));

  // Notes on the sheet:
  //   1 for writing WriteData to RAM 
  //   ALU operation
  //   1 for computed PC values, eg branch targets
  //   1 for using RAM ReadData, else ALUResult
  //   0 for using RD2 1 for ExtImm as ALU SrcB
  //   select which kind of imm exension to ExtImm
  //   1 for RegisterFile write enable (WE3)
  //   select which instruction bits are used for RA2
endmodule

module Adder_1_bit (
  input  CarryIn,
  input  a,
  input  b,
  output CarryOut,
  output Sum
);

  wire and_1_out, and_2_out, and_3_out, and_4_out, and_5_out, and_6_out, and_7_out;

  and and_1 (and_1_out, CarryIn, a);
  and and_2 (and_2_out, CarryIn, b);
  and and_3 (and_3_out, a, b);
  and and_4 (and_4_out, a, ~b, ~CarryIn);  // AND_Gate
  and and_5 (and_5_out, ~a, b, ~CarryIn);  // AND_Gate
  and and_6 (and_6_out, ~a, ~b, CarryIn);  // AND_Gate
  and and_7 (and_7_out, a, b, CarryIn);
  or or_1 (CarryOut, and_1_out, and_2_out, and_3_out);
  or or_2 (Sum, and_4_out, and_5_out, and_6_out, and_7_out);
endmodule

module Adder_32_bit (
  input  CarryIn,
  input  [31:0] A,
  input  [31:0] B,
  output [31:0] Sum,
  output CarryOut
);

  Adder #(.width(32)) adder_1 (.a(A), .b(B), .out(Sum), .cin(CarryIn), .cout(CarryOut));
endmodule

module Zero_Detect_32_bit (
  input  [31:0] A,
  output B
);

  nor nor_1 (B, A[0], A[1], A[2], A[3], A[4], A[5], A[6], A[7], A[8], A[9], A[10], A[11], A[12], A[13], A[14], A[15], A[16], A[17], A[18], A[19], A[20], A[21], A[22], A[23], A[24], A[25], A[26], A[27], A[28], A[29], A[30], A[31]);
endmodule

module RegisterSelect (
  input  [2:0] RegSel,
  input  [15:0] instr,
  output [3:0] RA1,
  output [3:0] RA2,
  output [3:0] RA3
);

  wire [2:0] multiplexer_1_out, multiplexer_2_out, multiplexer_3_out;

  Multiplexer #(.width(3)) multiplexer_1 (
    .in0(instr[8:6]), .in1(instr[10:8]), .out(multiplexer_1_out), .sel(RegSel[2]));
  Multiplexer #(.width(3)) multiplexer_2 (.in0(instr[2:0]), .in1(instr[5:3]), .out(multiplexer_2_out), .sel(RegSel[0]));
  Multiplexer #(.width(3)) multiplexer_3 (
    .in0(instr[5:3]), .in1(instr[10:8]), .out(multiplexer_3_out), .sel(RegSel[1]));
  assign RA1 = {{1{1'b0}}, multiplexer_2_out};  // Bit_Extender bit_extender_1
  assign RA2 = {{1{1'b0}}, multiplexer_3_out};  // Bit_Extender bit_extender_2
  assign RA3 = {{1{1'b0}}, multiplexer_1_out};  // Bit_Extender bit_extender_3

  // Notes on the sheet:
  //   000 is like in ADDS <Rd>,<Rn>,<Rm>
  //   Rm
  //   Rn
  //   Rd
endmodule

module Thumb_Decompress (
  input  [15:0] Instruction,
  output [3:0] Cond,
  output [1:0] Op,
  output [5:0] Funct,
  output [3:0] Rd
);
endmodule
